# Fritzing sketch IoT (saved by Fritzing 0.9.3b)
breadboards: 1

parts:
  Part2 = RFID-RC522-v3
  Part1 = Adafruit T-Cobbler Plus [part_number="Adafruit #1989 and #2028"]
  LCD1 = LCD screen
  LCM1602_IIC1 = LCM1602 IIC [part_number="LCM1602 IIC" chip_label="LCM1602 IIC" package="DIP (Dual Inline) [THT]"]
  PIR1 = PIR sensor
  DHT1 = DHT11 Humitidy and Temperature Sensor
  R1 = Resistor [tolerance=±5% resistance=10k package=THT]
  LED1 = LED - 3mm [color="Red (633nm)" package="3 mm [THT]"]
  R2 = Resistor [tolerance=±5% resistance=330 package=THT]
  J1 = Buzzer
  ADC1 = MCP3008 [package=dil16]
  R3 = PHOTOCELL [package=photocell-kit]
  R4 = Resistor [tolerance=±5% resistance=10k package=THT]

nets:
  N1: Part2.SDA, Part1.CE1
  N2: Part2.SCK, Part1.SCLK, ADC1.CLK
  N3: Part2.MOSI, Part1.MOSI, ADC1.Din
  N4: Part2.MISO, Part1.MISO, ADC1.Dout
  GND: Part2.GND, Part1.GND, LCM1602_IIC1.GND, PIR1.GND, DHT1.GND, R2.Pin_1, J1.pin1
  N5: Part2.RST, Part1.GPIO25
  VDD: Part2.3.3V, Part1.+3.3V, PIR1.VDD, DHT1.VDD, R1.Pin_0, ADC1.VREF, ADC1.VDD, R4.Pin_0
  N6: Part1.SDA, LCM1602_IIC1.SDA
  N7: Part1.SCL, LCM1602_IIC1.SCL
  N8: Part1.GPIO4, DHT1.DATA, R1.Pin_1
  N9: Part1.GPIO26, PIR1.SIG
  +5V: Part1.+5V, LCM1602_IIC1.VCC
  N10: Part1.GPIO24, LED1.anode
  N11: Part1.CE0, ADC1.CS/SHDN
  N12: Part1.GPIO21, J1.pin2
  VSS: LCD1.VSS, LCM1602_IIC1.VSS
  VDD_2: LCD1.VDD, LCM1602_IIC1.VDD
  N13: LCD1.V0, LCM1602_IIC1.V0
  N14: LCD1.RS, LCM1602_IIC1.RS
  N15: LCD1.R/W, LCM1602_IIC1.RW
  N16: LCD1.E, LCM1602_IIC1.E
  N17: LCD1.DB0, LCM1602_IIC1.D0
  N18: LCD1.DB1, LCM1602_IIC1.D1
  N19: LCD1.DB2, LCM1602_IIC1.D2
  N20: LCD1.DB3, LCM1602_IIC1.D3
  N21: LCD1.DB4, LCM1602_IIC1.D4
  N22: LCD1.DB5, LCM1602_IIC1.D5
  N23: LCD1.DB6, LCM1602_IIC1.D6
  N24: LCD1.DB7, LCM1602_IIC1.D7
  N25: LCD1.LED+, LCM1602_IIC1.A
  N26: LCD1.LED-, LCM1602_IIC1.K
  N27: LCM1602_IIC1.LED_A, LCM1602_IIC1.LED_B
  N28: LED1.cathode, R2.Pin_0
  N29: ADC1.CH0, R3.P$1, R4.Pin_1
  N30: ADC1.DGND, ADC1.AGND, R3.P$2

custom parts:
  RFID-RC522-v3: A simple China made RFID-RC522 Reader (6x4 cm); do check the pin labels, as this is a MFRC522 based clone.
  Adafruit T-Cobbler Plus: The Raspberry Pi has landed on the Maker World like a 40-GPIO pinned, quad-USB ported, credit card sized bomb of DIY joy. And while you can use most of our great Model B accessories by hooking up our downgrade cable, its probably a good time to upgrade your set up and accessorize using all of the 40 pins. That's why we now carry the Assembled Adafruit Pi T-Cobbler Plus - Breakout + Cable for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
  LCM1602 IIC: I2C-Module to use a 1602 or 2004 LCD on with the wire.h libory Serial LCD Modul
  DHT11 Humitidy and Temperature Sensor: DHT11 Humidity and Temperature Sensor
  Buzzer: Fixed frequency buzzer
